// Logisim project 2-bit_register.circ as structural Verilog: 1 circuit, main circuit main
module main (
  input  in_1,
  input  D,
  input  D_2,
  output Q,
  output Q_prime,
  output Q_2,
  output Q_prime_2
);

  wire and_1_out, and_2_out, and_3_out, and_4_out, and_5_out, and_6_out, and_7_out, and_8_out, and_9_out,
       and_10_out, and_11_out, and_12_out, clock_1_out, nor_1_out, nor_2_out, nor_3_out, nor_4_out,
       not_1_out, not_2_out, not_3_out, not_4_out;

  Clock clock_1 (.out(clock_1_out));
  not not_1 (not_1_out, D);
  not not_2 (not_2_out, D_2);
  and and_1 (and_1_out, in_1, D);
  and and_2 (and_2_out, not_1_out, in_1);
  and and_3 (and_3_out, in_1, D_2);
  and and_4 (and_4_out, not_2_out, in_1);
  and and_5 (and_5_out, Q_prime, and_1_out, clock_1_out);
  and and_6 (and_6_out, clock_1_out, and_2_out, Q);
  and and_7 (and_7_out, Q_prime_2, and_3_out, clock_1_out);
  and and_8 (and_8_out, clock_1_out, and_4_out, Q_2);
  nor nor_1 (nor_1_out, and_5_out, nor_2_out);
  nor nor_2 (nor_2_out, nor_1_out, and_6_out);
  not not_3 (not_3_out, clock_1_out);
  nor nor_3 (nor_3_out, and_7_out, nor_4_out);
  nor nor_4 (nor_4_out, nor_3_out, and_8_out);
  not not_4 (not_4_out, clock_1_out);
  and and_9 (and_9_out, nor_1_out, not_3_out);
  and and_10 (and_10_out, not_3_out, nor_2_out);
  and and_11 (and_11_out, nor_3_out, not_4_out);
  and and_12 (and_12_out, not_4_out, nor_4_out);
  nor nor_5 (Q, and_9_out, Q_prime);
  nor nor_6 (Q_prime, Q, and_10_out);
  nor nor_7 (Q_2, and_11_out, Q_prime_2);
  nor nor_8 (Q_prime_2, Q_2, and_12_out);
endmodule
