// Logisim project JK_counter.circ as structural Verilog: 1 circuit, main circuit main
module main (
  input  K,
  output Q,
  output Q_prime,
  output Q_2,
  output Q_prime_2
);

  wire and_1_out, and_2_out, and_3_out, and_4_out, and_5_out, and_6_out, and_7_out, and_8_out, clock_1_out,
       nor_1_out, nor_2_out, nor_3_out, nor_4_out, not_1_out, not_2_out, undriven;
  wire [15:0] counter_1_q;

  Clock clock_1 (.out(clock_1_out));
  Counter #(.width(16), .max('hffff)) counter_1 (.Q(counter_1_q), .clr(undriven));  // open: load, D, count, carry, clk
  and and_1 (and_1_out, Q_prime, K, clock_1_out);
  and and_2 (and_2_out, clock_1_out, K, Q);
  and and_3 (and_3_out, Q_prime_2, K, Q);
  and and_4 (and_4_out, Q, K, Q_2);
  nor nor_1 (nor_1_out, and_1_out, nor_2_out);
  nor nor_2 (nor_2_out, nor_1_out, and_2_out);
  not not_1 (not_1_out, clock_1_out);
  nor nor_3 (nor_3_out, and_3_out, nor_4_out);
  nor nor_4 (nor_4_out, nor_3_out, and_4_out);
  not not_2 (not_2_out, Q);
  and and_5 (and_5_out, nor_1_out, not_1_out);
  and and_6 (and_6_out, not_1_out, nor_2_out);
  and and_7 (and_7_out, nor_3_out, not_2_out);
  and and_8 (and_8_out, not_2_out, nor_4_out);
  nor nor_5 (Q, and_5_out, Q_prime);
  nor nor_6 (Q_prime, Q, and_6_out);
  nor nor_7 (Q_2, and_7_out, Q_prime_2);
  nor nor_8 (Q_prime_2, Q_2, and_8_out);

  // Notes on the sheet:
  //   Y1
  //   Y2
endmodule
