// Logisim project arithm_1.circ as structural Verilog: 1 circuit, main circuit main
module main (
  input  [7:0] in_1,
  input  in_2,
  input  \АДР_РЕГ ,
  input  in_4,
  input  \ВЫХ_АРИФМ ,
  input  \РОН_А ,
  input  \РОН_Б ,
  input  \ВЫЧ ,
  output [7:0] \ШИНА 
);

  wire clock_1_out;
  wire [3:0] bit_extender_1_out, \АДР_РЕГ_q ;
  wire [7:0] adder_1_out, xor_1_out, \РОН_А_q , \РОН_Б_q ;

  Clock clock_1 (.out(clock_1_out));
  assign \ШИНА  = in_2 ? in_1 : 8'bz;  // Controlled_Buffer controlled_buffer_1
  Bit_Extender #(.out_width(4)) bit_extender_1 (.in(\ШИНА ), .out(bit_extender_1_out));
  assign \ШИНА  = \ВЫХ_АРИФМ  ? adder_1_out : 8'bz;  // Controlled_Buffer controlled_buffer_2
  Pull_Resistor pull_resistor_1 (.node(\ШИНА ));
  Register #(.width(4)) \u_АДР_РЕГ  (
    .D(bit_extender_1_out), .en(\АДР_РЕГ ), .Q(\АДР_РЕГ_q ), .clk(clock_1_out), .clr(in_4));
  Register \u_РОН_А  (.D(\ШИНА ), .en(\РОН_А ), .Q(\РОН_А_q ), .clk(clock_1_out), .clr(in_4));
  Register \u_РОН_Б  (.D(\ШИНА ), .en(\РОН_Б ), .Q(\РОН_Б_q ), .clk(clock_1_out), .clr(in_4));
  assign xor_1_out = \РОН_Б_q  ^ {8{\ВЫЧ }};  // XOR_Gate xor_1, 8 bits wide
  Adder adder_1 (.a(\РОН_А_q ), .b(xor_1_out), .out(adder_1_out), .cin(\ВЫЧ ));  // open: cout
endmodule
