// Logisim project base_JK.circ as structural Verilog: 1 circuit, main circuit main
module main (
  input  EN,
  input  J,
  input  K,
  output Q,
  output Q_prime
);

  wire and_1_out, and_2_out;

  and and_1 (and_1_out, Q, EN, J);
  and and_2 (and_2_out, K, EN, Q_prime);
  nor nor_1 (Q, and_1_out, Q_prime);
  nor nor_2 (Q_prime, Q, and_2_out);
endmodule
