// Logisim project comp_1.circ as structural Verilog: 1 circuit, main circuit main
module main (
  input  [7:0] in_1,
  input  in_2,
  input  \СЧЁТ ,
  input  \ВЫХ_С_И ,
  input  \ВХОД_А_Р ,
  input  \ВКЛ_ОЗУ ,
  input  \СБРОС_ПАМ ,
  input  \ЧТ_ОЗУ ,
  input  \СБРОС_РЕГ ,
  input  \РОН_А ,
  input  \РОН_Б ,
  input  \ВЫЧ ,
  input  \АРИФМ ,
  output [7:0] \ШИНА 
);

  wire clock_1_out;
  wire [3:0] bit_extender_2_out, counter_1_q, \АДР_РЕГ_q ;
  wire [7:0] adder_1_out, bit_extender_1_out, xor_1_out, \РОН_А_q , \РОН_Б_q ;

  Clock clock_1 (.out(clock_1_out));
  Counter #(.width(4), .max('hf)) counter_1 (
    .count(\СЧЁТ ), .Q(counter_1_q), .clk(clock_1_out), .clr(\СБРОС_РЕГ ));  // open: load, D, carry
  assign \ШИНА  = \ВЫХ_С_И  ? bit_extender_1_out : 8'bz;  // Controlled_Buffer controlled_buffer_1
  assign bit_extender_1_out = {{4{1'b0}}, counter_1_q};  // Bit_Extender bit_extender_1
  assign \ШИНА  = in_2 ? in_1 : 8'bz;  // Controlled_Buffer controlled_buffer_2
  assign \ШИНА  = \АРИФМ  ? adder_1_out : 8'bz;  // Controlled_Buffer controlled_buffer_3
  Pull_Resistor pull_resistor_1 (.node(\ШИНА ));
  Bit_Extender #(.out_width(4)) bit_extender_2 (.in(\ШИНА ), .out(bit_extender_2_out));
  Register #(.width(4)) \u_АДР_РЕГ  (
    .D(bit_extender_2_out), .en(\ВХОД_А_Р ), .Q(\АДР_РЕГ_q ), .clk(clock_1_out), .clr(\СБРОС_РЕГ ));
  Register \u_РОН_А  (.D(\ШИНА ), .en(\РОН_А ), .Q(\РОН_А_q ), .clk(clock_1_out), .clr(\СБРОС_РЕГ ));
  Register \u_РОН_Б  (.D(\ШИНА ), .en(\РОН_Б ), .Q(\РОН_Б_q ), .clk(clock_1_out), .clr(\СБРОС_РЕГ ));
  assign xor_1_out = \РОН_Б_q  ^ {8{\ВЫЧ }};  // XOR_Gate xor_1, 8 bits wide
  Adder adder_1 (.a(\РОН_А_q ), .b(xor_1_out), .out(adder_1_out), .cin(\ВЫЧ ));  // open: cout
  RAM #(.addrWidth(4)) ram_1 (
    .addr(\АДР_РЕГ_q ), .data(\ШИНА ), .sel(\ВКЛ_ОЗУ ), .clk(clock_1_out), .ld(\ЧТ_ОЗУ ), .clr(\СБРОС_ПАМ ));
endmodule
