// Logisim project comp_2.circ as structural Verilog: 1 circuit, main circuit main
module main (
  input  [7:0] in_1,
  input  in_2,
  input  \ВХ_С_И ,
  input  \СЧЁТ ,
  input  \ВЫХ_С_И ,
  input  \ВХОД_А_Р ,
  input  \ВКЛ_ОЗУ ,
  input  \СБРОС_ПАМ ,
  input  \ЧТ_ОЗУ ,
  input  \СБРОС_РЕГ ,
  input  \ВХ_Р_И ,
  input  \ВЫХ_Р_И ,
  input  \РОН_А ,
  input  \РОН_Б ,
  input  \ВЫЧ ,
  input  \АРИФМ ,
  output [7:0] \ШИНА 
);

  wire clock_1_out, not_1_out;
  wire [2:0] counter_1_q;
  wire [3:0] bit_extender_3_out, \АДР_РЕГ_q , \СЧТ_ИН_q ;
  wire [7:0] adder_1_out, bit_extender_1_out, bit_extender_2_out, xor_1_out, \РЕГ_ИНСТР_q , \РОН_А_q ,
       \РОН_Б_q ;

  Register \u_РЕГ_ИНСТР  (.D(\ШИНА ), .en(\ВХ_Р_И ), .Q(\РЕГ_ИНСТР_q ), .clk(clock_1_out), .clr(\СБРОС_РЕГ ));
  Clock clock_1 (.out(clock_1_out));
  Counter #(.width(4), .max('hf)) \u_СЧТ_ИН  (
    .load(\ВХ_С_И ), .count(\СЧЁТ ), .Q(\СЧТ_ИН_q ), .clk(clock_1_out), .clr(\СБРОС_РЕГ ));  // open: D, carry
  Counter #(.width(3), .max('h7)) counter_1 (
    .Q(counter_1_q), .clk(not_1_out), .clr(\СБРОС_РЕГ ));  // open: load, D, count, carry
  assign \ШИНА  = in_2 ? in_1 : 8'bz;  // Controlled_Buffer controlled_buffer_1
  assign bit_extender_1_out = {{4{1'b0}}, \СЧТ_ИН_q };  // Bit_Extender bit_extender_1
  assign \ШИНА  = \ВЫХ_С_И  ? bit_extender_1_out : 8'bz;  // Controlled_Buffer controlled_buffer_2
  assign \ШИНА  = \ВЫХ_Р_И  ? bit_extender_2_out : 8'bz;  // Controlled_Buffer controlled_buffer_3
  assign bit_extender_2_out = {{4{1'b0}}, \РЕГ_ИНСТР_q [3:0]};  // Bit_Extender bit_extender_2
  not not_1 (not_1_out, clock_1_out);
  Bit_Extender #(.out_width(4)) bit_extender_3 (.in(\ШИНА ), .out(bit_extender_3_out));
  assign \ШИНА  = \АРИФМ  ? adder_1_out : 8'bz;  // Controlled_Buffer controlled_buffer_4
  Pull_Resistor pull_resistor_1 (.node(\ШИНА ));
  Register #(.width(4)) \u_АДР_РЕГ  (
    .D(bit_extender_3_out), .en(\ВХОД_А_Р ), .Q(\АДР_РЕГ_q ), .clk(clock_1_out), .clr(\СБРОС_РЕГ ));
  Register \u_РОН_А  (.D(\ШИНА ), .en(\РОН_А ), .Q(\РОН_А_q ), .clk(clock_1_out), .clr(\СБРОС_РЕГ ));
  Register \u_РОН_Б  (.D(\ШИНА ), .en(\РОН_Б ), .Q(\РОН_Б_q ), .clk(clock_1_out), .clr(\СБРОС_РЕГ ));
  assign xor_1_out = \РОН_Б_q  ^ {8{\ВЫЧ }};  // XOR_Gate xor_1, 8 bits wide
  ROM #(.addrWidth(7), .dataWidth(12)) rom_1 (.addr({\РЕГ_ИНСТР_q [7:4], counter_1_q}));  // open: data, sel
  RAM #(.addrWidth(4)) ram_1 (
    .addr(\АДР_РЕГ_q ), .data(\ШИНА ), .sel(\ВКЛ_ОЗУ ), .clk(clock_1_out), .ld(\ЧТ_ОЗУ ), .clr(\СБРОС_ПАМ ));
  Adder adder_1 (.a(\РОН_А_q ), .b(xor_1_out), .out(adder_1_out), .cin(\ВЫЧ ));  // open: cout

  // Notes on the sheet:
  //   contents of rom_1 (hex, n*v repeats v):
  //   50*0 a5
endmodule
