// Logisim project comp_5.circ as structural Verilog: 1 circuit, main circuit main
module main (
  input  [7:0] in_1,
  input  in_2,
  input  \СБРОС_ПАМ ,
  input  \СБРОС_РЕГ ,
  output [7:0] \ШИНА 
);

  wire clock_1_out, nor_1_out, not_1_out, or_1_out, \АРИФМ , \ВКЛ_ОЗУ , \ВХ_Р_И , \ВХ_Р_Н , \ВХ_С_И ,
       \ВХОД_А_Р , \ВЫХ_Р_А , \ВЫХ_Р_И , \ВЫХ_Р_Н , \ВЫХ_С_И , \ВЫЧ , \РОН_А , \РОН_Б , \СБР_Р_Н , \СЧЁТ ,
       \ЧТ_ОЗУ ;
  wire [2:0] counter_1_q;
  wire [3:0] bit_extender_3_out, \АДР_РЕГ_q , \СЧТ_ИН_q ;
  wire [7:0] adder_1_out, bit_extender_1_out, bit_extender_2_out, xor_1_out, \РЕГ_ИНСТР_q , \РОН_А_q ,
       \РОН_Б_q ;

  Register \u_РЕГ_ИНСТР  (.D(\ШИНА ), .en(\ВХ_Р_И ), .Q(\РЕГ_ИНСТР_q ), .clk(clock_1_out), .clr(\СБРОС_РЕГ ));
  Clock clock_1 (.out(clock_1_out));
  Counter #(.width(4), .max('hf)) \u_СЧТ_ИН  (
    .load(\ВХ_С_И ), .D(bit_extender_3_out), .count(\СЧЁТ ), .Q(\СЧТ_ИН_q ), .clk(clock_1_out),
    .clr(\СБРОС_РЕГ ));  // open: carry
  Counter #(.width(3), .max('h7)) counter_1 (
    .Q(counter_1_q), .clk(not_1_out), .clr(\СБРОС_РЕГ ));  // open: load, D, count, carry
  assign \ШИНА  = in_2 ? in_1 : 8'bz;  // Controlled_Buffer controlled_buffer_1
  assign \ШИНА  = \ВЫХ_С_И  ? bit_extender_1_out : 8'bz;  // Controlled_Buffer controlled_buffer_2
  assign bit_extender_1_out = {{4{1'b0}}, \СЧТ_ИН_q };  // Bit_Extender bit_extender_1
  assign bit_extender_2_out = {{4{1'b0}}, \РЕГ_ИНСТР_q [3:0]};  // Bit_Extender bit_extender_2
  assign \ШИНА  = \ВЫХ_Р_И  ? bit_extender_2_out : 8'bz;  // Controlled_Buffer controlled_buffer_3
  not not_1 (not_1_out, clock_1_out);
  Bit_Extender #(.out_width(4)) bit_extender_3 (.in(\ШИНА ), .out(bit_extender_3_out));
  assign \ШИНА  = \АРИФМ  ? adder_1_out : 8'bz;  // Controlled_Buffer controlled_buffer_4
  assign \ШИНА  = \ВЫХ_Р_А  ? \РОН_А_q  : 8'bz;  // Controlled_Buffer controlled_buffer_5
  Pull_Resistor pull_resistor_1 (.node(\ШИНА ));
  Register #(.width(4)) \u_АДР_РЕГ  (
    .D(bit_extender_3_out), .en(\ВХОД_А_Р ), .Q(\АДР_РЕГ_q ), .clk(clock_1_out), .clr(\СБРОС_РЕГ ));
  Register \u_РОН_А  (.D(\ШИНА ), .en(\РОН_А ), .Q(\РОН_А_q ), .clk(clock_1_out), .clr(\СБРОС_РЕГ ));
  Register \u_РОН_Б  (.D(\ШИНА ), .en(\РОН_Б ), .Q(\РОН_Б_q ), .clk(clock_1_out), .clr(\СБРОС_РЕГ ));
  nor nor_1 (nor_1_out, adder_1_out[0], adder_1_out[1], adder_1_out[2], adder_1_out[3], adder_1_out[4], adder_1_out[5], adder_1_out[6], adder_1_out[7]);
  assign xor_1_out = \РОН_Б_q  ^ {8{\ВЫЧ }};  // XOR_Gate xor_1, 8 bits wide
  ROM #(.dataWidth(15)) rom_1 (
    .addr({\ВЫХ_Р_Н , \РЕГ_ИНСТР_q [7:4], counter_1_q}),
    .data({\СБР_Р_Н , \ВХ_Р_Н , \ВЫХ_Р_А , \ВХ_С_И , \СЧЁТ , \ВЫХ_С_И , \ВХОД_А_Р , \ВКЛ_ОЗУ , \ЧТ_ОЗУ , \ВХ_Р_И , \ВЫХ_Р_И , \РОН_А , \РОН_Б , \ВЫЧ , \АРИФМ }));  // open: sel
  RAM #(.addrWidth(4)) ram_1 (
    .addr(\АДР_РЕГ_q ), .data(\ШИНА ), .sel(\ВКЛ_ОЗУ ), .clk(clock_1_out), .ld(\ЧТ_ОЗУ ), .clr(\СБРОС_ПАМ ));
  Adder adder_1 (.a(\РОН_А_q ), .b(xor_1_out), .out(adder_1_out), .cin(\ВЫЧ ));  // open: cout
  Register #(.width(1)) register_1 (.D(nor_1_out), .en(\ВХ_Р_Н ), .Q(\ВЫХ_Р_Н ), .clk(clock_1_out), .clr(or_1_out));
  or or_1 (or_1_out, \СБРОС_РЕГ , \СБР_Р_Н );

  // Notes on the sheet:
  //   contents of rom_1 (hex, n*v repeats v):
  //   300 e0 400 5*0 300 e0 110 c8 400 0 0 0 300 e0 110 c4 2009 400 0 0 300 e0 110 c4 200b 400 0 0 300 e0
  //   110 1080 400 0 0 0 300 e0 18 400 4*0 300 e0 810 5*0 300 e0 400 61*0 300 e0 6*0 300 e0 400 5*0 300 e0
  //   110 c8 400 0 0 0 300 e0 110 c4 2009 400 0 0 300 e0 110 c4 200b 400 0 0 300 e0 110 1080 400 0 0 0 300
  //   e0 18 400 4*0 300 e0 810 5*0 300 e0 810 4000 60*0 300 e0
endmodule
