// Logisim project mul4.circ as structural Verilog: 1 circuit, main circuit main
module main (
  input  [3:0] in_1,
  input  [3:0] in_2,
  output [7:0] out_3
);

  wire [3:0] and_2_out, and_3_out, and_4_out;
  wire [3:1] adder_1_out, adder_2_out, and_1_out;
  wire [3:3] adder_1_cout, adder_2_cout, pull_resistor_1_node;

  assign {and_1_out, out_3[0]} = in_1 & {4{in_2[0]}};  // AND_Gate and_1, 4 bits wide
  Pull_Resistor pull_resistor_1 (.node(pull_resistor_1_node[3]));
  assign and_2_out = in_1 & {4{in_2[1]}};  // AND_Gate and_2, 4 bits wide
  Adder #(.width(4)) adder_1 (
    .a({pull_resistor_1_node[3], and_1_out}), .b(and_2_out), .out({adder_1_out, out_3[1]}),
    .cout(adder_1_cout[3]));  // open: cin
  assign and_3_out = in_1 & {4{in_2[2]}};  // AND_Gate and_3, 4 bits wide
  Adder #(.width(4)) adder_2 (
    .a({adder_1_cout[3], adder_1_out}), .b(and_3_out), .out({adder_2_out, out_3[2]}), .cout(adder_2_cout[3]));  // open: cin
  assign and_4_out = in_1 & {4{in_2[3]}};  // AND_Gate and_4, 4 bits wide
  Adder #(.width(4)) adder_3 (
    .a({adder_2_cout[3], adder_2_out}), .b(and_4_out), .out(out_3[6:3]), .cout(out_3[7]));  // open: cin
endmodule
