// Logisim project sum.circ as structural Verilog: 1 circuit, main circuit main
module main (
  input  Ci,
  input  A,
  input  B,
  input  C0in,
  input  A0,
  input  B0,
  input  A1,
  input  B1,
  input  Cin,
  input  [7:0] A_2,
  input  [7:0] B_2,
  output Y0,
  output C0out,
  output Y,
  output C1in,
  output Y1,
  output C1out,
  output Co,
  output [7:0] Y_2,
  output Cout
);

  wire and_1_out, and_2_out, and_3_out, and_4_out, and_5_out, and_6_out, and_7_out, and_8_out, not_1_out,
       not_2_out, not_3_out;

  not not_1 (not_1_out, Ci);
  not not_2 (not_2_out, A);
  not not_3 (not_3_out, B);
  and and_1 (and_1_out, A, not_3_out, not_1_out);
  and and_2 (and_2_out, B, not_2_out, not_1_out);
  and and_3 (and_3_out, Ci, not_2_out, not_3_out);
  and and_4 (and_4_out, A, B, Ci);
  and and_5 (and_5_out, A, B, not_1_out);
  and and_6 (and_6_out, A, Ci, not_3_out);
  and and_7 (and_7_out, B, Ci, not_2_out);
  and and_8 (and_8_out, A, B, Ci);
  or or_1 (Y, and_1_out, and_2_out, and_3_out, and_4_out);
  or or_2 (Co, and_5_out, and_6_out, and_7_out, and_8_out);
  Adder #(.width(1)) adder_1 (.a(A0), .b(B0), .out(Y0), .cin(C0in), .cout(C0out));
  Adder #(.width(1)) adder_2 (.a(A1), .b(B1), .out(Y1), .cin(C0out), .cout(C1out));
  Adder adder_3 (.a(A_2), .b(B_2), .out(Y_2), .cin(Cin), .cout(Cout));

  assign C1in = C0out;
endmodule
