// Logisim project tri-state_buf.circ as structural Verilog: 1 circuit, main circuit main
module main (
  input  in_1,
  input  \ВХОД ,
  input  \ВКЛ ,
  output \ВЫХОД 
);

  wire not_1_out, not_2_out, pull_resistor_1_node, transistor_1_out, transistor_4_out;

  not not_1 (not_1_out, \ВХОД );
  not not_2 (not_2_out, \ВКЛ );
  Pull_Resistor #(.pull(1)) pull_resistor_1 (.node(pull_resistor_1_node));
  Transistor transistor_1 (.in(pull_resistor_1_node), .out(transistor_1_out), .gate(not_2_out));
  Transistor transistor_2 (.in(transistor_1_out), .out(\ВЫХОД ), .gate(not_1_out));
  Transistor #(.\type ("n")) transistor_3 (.in(transistor_4_out), .out(\ВЫХОД ), .gate(not_1_out));
  Transistor #(.\type ("n")) transistor_4 (.in(1'b0), .out(transistor_4_out), .gate(\ВКЛ ));
  Pull_Resistor pull_resistor_2 (.node(\ВЫХОД ));
endmodule
