// Logisim project лог_вентили.circ as structural Verilog: 1 circuit, main circuit main
module main (
  input  \И ,
  input  in_2,
  input  in_3,
  input  in_4,
  input  in_5,
  input  in_6,
  input  in_7,
  input  in_8,
  input  in_9,
  input  in_10,
  input  in_11,
  input  in_12,
  input  in_13,
  input  in_14,
  output out_15,
  output out_16,
  output out_17,
  output out_18,
  output out_19,
  output out_20,
  output out_21,
  output out_22
);

  wire pull_resistor_5_node, transistor_1_out, transistor_4_out, transistor_10_out, transistor_15_out,
       transistor_16_out;

  Transistor #(.\type ("n")) transistor_1 (.in(1'b1), .out(transistor_1_out), .gate(\И ));
  Transistor #(.\type ("n")) transistor_2 (.in(transistor_1_out), .out(out_16), .gate(in_5));
  Pull_Resistor pull_resistor_1 (.node(out_16));
  Pull_Resistor #(.pull(1)) pull_resistor_2 (.node(out_19));
  Transistor #(.\type ("n")) transistor_3 (.in(transistor_4_out), .out(out_19), .gate(in_9));
  Transistor #(.\type ("n")) transistor_4 (.in(1'b0), .out(transistor_4_out), .gate(in_11));
  Transistor #(.\type ("n")) transistor_5 (.in(1'b1), .out(out_17), .gate(in_2));
  Transistor #(.\type ("n")) transistor_6 (.in(1'b1), .out(out_17), .gate(in_6));
  Pull_Resistor pull_resistor_3 (.node(out_17));
  Pull_Resistor #(.pull(1)) pull_resistor_4 (.node(out_20));
  Transistor #(.\type ("n")) transistor_7 (.in(1'b0), .out(out_20), .gate(in_10));
  Transistor #(.\type ("n")) transistor_8 (.in(1'b0), .out(out_20), .gate(in_12));
  Pull_Resistor #(.pull(1)) pull_resistor_5 (.node(pull_resistor_5_node));
  Transistor #(.\type ("n")) transistor_9 (.in(transistor_10_out), .out(pull_resistor_5_node), .gate(in_3));
  Transistor #(.\type ("n")) transistor_10 (.in(1'b0), .out(transistor_10_out), .gate(in_7));
  Transistor #(.\type ("n")) transistor_11 (.in(pull_resistor_5_node), .out(out_18), .gate(in_3));
  Pull_Resistor pull_resistor_6 (.node(out_18));
  Transistor #(.\type ("n"), .gate("br")) transistor_12 (.in(pull_resistor_5_node), .out(out_18), .gate(in_7));
  Pull_Resistor #(.pull(1)) pull_resistor_7 (.node(out_21));
  Transistor #(.\type ("n")) transistor_13 (.in(1'b0), .out(out_21), .gate(in_13));
  Transistor #(.\type ("n")) transistor_14 (.in(transistor_16_out), .out(out_15), .gate(in_4));
  Transistor #(.\type ("n")) transistor_15 (.in(1'b1), .out(transistor_15_out), .gate(in_4));
  Transistor #(.\type ("n")) transistor_16 (.in(transistor_15_out), .out(transistor_16_out), .gate(in_8));
  Pull_Resistor pull_resistor_8 (.node(transistor_16_out));
  Transistor #(.\type ("n")) transistor_17 (.in(1'b1), .out(out_22), .gate(in_14));
  Pull_Resistor pull_resistor_9 (.node(out_22));
  Pull_Resistor #(.pull(1)) pull_resistor_10 (.node(out_15));
  Transistor #(.\type ("n"), .gate("br")) transistor_18 (.in(transistor_16_out), .out(out_15), .gate(in_8));

  // Notes on the sheet:
  //   И-НЕ
  //   ИЛИ
  //   ИЛИ-НЕ
endmodule
